# Fritzing sketch circuito_taller_nubes_y_antenas (saved by Fritzing 0.9.4)
circuit board: 7.5cm x 7.5cm
breadboards: 1

parts:
  LED1 = LED - 3mm [color="Red (633nm)" package="3 mm [THT]"]
  LED2 = LED - 3mm [color="Red (633nm)" package="3 mm [THT]"]
  LED3 = LED - 3mm [color="Red (633nm)" package="3 mm [THT]"]
  LED4 = LED - 3mm [color="Red (633nm)" package="3 mm [THT]"]
  R1 = Resistor [tolerance=±5% resistance=220 package=THT]
  R2 = Resistor [tolerance=±5% resistance=220 package=THT]
  R3 = Resistor [tolerance=±5% resistance=220 package=THT]
  R4 = Resistor [tolerance=±5% resistance=220 package=THT]
  microSD1 = MicroSD Card Module
  JP1 = Header 6 [package=molex-1x6-ra]
  esp1 = ESP32 DevKitc V4
  U1 = EM406 GPS Connector [package=em406]

nets:
  N1: LED1.cathode, LED2.cathode, LED3.cathode, LED4.cathode, esp1.GND#32
  N2: LED1.anode, R1.Pin_1
  N3: LED2.anode, R2.Pin_1
  N4: LED3.anode, R3.Pin_1
  N5: LED4.anode, R4.Pin_1
  N6: R1.Pin_0, esp1.IO12
  N7: R2.Pin_0, esp1.IO14
  N8: R3.Pin_0, esp1.IO27
  N9: R4.Pin_0, esp1.IO26
  N10: microSD1.GND, esp1.GND#12
  VCC: microSD1.VCC, JP1.5, esp1.5V, U1.VCC
  N11: microSD1.MISO, esp1.IO19
  N12: microSD1.MOSI, esp1.IO23
  N13: microSD1.SCK, esp1.IO18
  N14: microSD1.CS, esp1.IO5
  N15: JP1.3, esp1.IO16, U1.TX
  N16: JP1.4, esp1.IO17, U1.RX
  N17: JP1.6, esp1.GND#18, U1.GND1

custom parts:
  ESP32 DevKitc V4: ESP32-DevKitC board with ESP32-WROOM-32 module. ESP32-DevKitC V4 is a small-sized ESP32-based development board produced by Espressif. Most of the pins on the ESP module are broken out to the pin headers on the board. The pins D0, D1, D2, D3, CMD and CLK are used internally for communication between ESP32 and SPI flash memory. They are grouped on both sides near the USB connector. Avoid using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
